# Fritzing sketch city light sensor (saved by Fritzing 0.9.3b)
breadboards: 1

parts:
  Εξάρτημα1 = Arduino Mega ADK (Rev3)
  e-radionica_com1 = LM393 LDR breakout [part_number=100027]

nets:
  N1: Εξάρτημα1.A10, e-radionica_com1.AO
  5V: Εξάρτημα1.5V, e-radionica_com1.VCC
  GND: Εξάρτημα1.GND, e-radionica_com1.GND
