# Fritzing sketch city lights (saved by Fritzing 0.9.3b)
breadboards: 1

parts:
  Εξάρτημα1 = Arduino Mega ADK (Rev3)
  LED1 = LED - 5mm [color="Red (633nm)" package="5 mm [THT]"]
  LED2 = LED - 5mm [color="Red (633nm)" package="5 mm [THT]"]
  LED3 = LED - 5mm [color="Red (633nm)" package="5 mm [THT]"]
  LED4 = LED - 5mm [color="Red (633nm)" package="5 mm [THT]"]
  LED5 = LED - 5mm [color="Red (633nm)" package="5 mm [THT]"]
  LED6 = LED - 5mm [color="Red (633nm)" package="5 mm [THT]"]
  WhiteLEDmodule1 = WhiteLEDmodule
  R1 = Resistor [tolerance=±5% resistance=220 package=THT]
  R2 = Resistor [tolerance=±5% resistance=220 package=THT]
  R3 = Resistor [tolerance=±5% resistance=220 package=THT]
  R4 = Resistor [tolerance=±5% resistance=220 package=THT]
  R5 = Resistor [tolerance=±5% resistance=220 package=THT]
  R6 = Resistor [tolerance=±5% resistance=220 package=THT]

nets:
  N1: Εξάρτημα1.5V, LED1.cathode, WhiteLEDmodule1.POWER
  N2: Εξάρτημα1.D36, R1.Pin_0
  N3: Εξάρτημα1.D38, R2.Pin_0
  N4: Εξάρτημα1.D40, R3.Pin_0
  N5: Εξάρτημα1.D42, R4.Pin_0
  N6: Εξάρτημα1.D44, R5.Pin_0
  N7: Εξάρτημα1.D46, R6.Pin_0
  N8: Εξάρτημα1.D48, WhiteLEDmodule1.INPUT
  GND: Εξάρτημα1.GND, LED2.cathode, LED3.cathode, LED4.cathode, LED5.anode, LED6.cathode, WhiteLEDmodule1.GND
  N9: LED1.anode, R1.Pin_1
  N10: LED2.anode, R2.Pin_1
  N11: LED3.anode, R3.Pin_1
  N12: LED4.anode, R4.Pin_1
  N13: LED5.cathode, R5.Pin_1
  N14: LED6.anode, R6.Pin_1
