# Fritzing sketch city sonars (saved by Fritzing 0.9.3b)
breadboards: 1

parts:
  Εξάρτημα1 = Arduino Mega ADK (Rev3)
  HC-SR04_Sensor_1 = HC-SR04 Ultrasonic Distance Sensor
  HC-SR04_Sensor_2 = HC-SR04 Ultrasonic Distance Sensor
  HC-SR04_Sensor_3 = HC-SR04 Ultrasonic Distance Sensor

nets:
  GND: Εξάρτημα1.GND, HC-SR04_Sensor_1.GND, HC-SR04_Sensor_2.GND, HC-SR04_Sensor_3.GND
  VCC: Εξάρτημα1.5V, HC-SR04_Sensor_1.VCC, HC-SR04_Sensor_2.VCC, HC-SR04_Sensor_3.VCC
  N1: Εξάρτημα1.D22, HC-SR04_Sensor_1.ECHO
  N2: Εξάρτημα1.D24, HC-SR04_Sensor_1.TRIG
  N3: Εξάρτημα1.D26, HC-SR04_Sensor_2.ECHO
  N4: Εξάρτημα1.D28, HC-SR04_Sensor_2.TRIG
  N5: Εξάρτημα1.D30, HC-SR04_Sensor_3.ECHO
  N6: Εξάρτημα1.D32, HC-SR04_Sensor_3.TRIG
