# Fritzing sketch city water pump (saved by Fritzing 0.9.3b)
breadboards: 1

parts:
  Εξάρτημα1 = Arduino Mega ADK (Rev3)
  KY-1 = Keyes Relay [package=THT]
  M1 = DC Motor
  Power_plug1 = Power plug

nets:
  N1: Εξάρτημα1.D12_PWM, KY-1.signal
  N2: Εξάρτημα1.5V, KY-1.power
  N3: Εξάρτημα1.GND, KY-1.ground
  N4: KY-1.C, Power_plug1.GND
  N5: KY-1.NO, M1.pin_2
  N6: M1.pin_1, Power_plug1.VCC

custom parts:
  Keyes Relay: The Keyes 5V relay module is suitable for SCM development, home appliance control. It uses a 5V~12V TIL control signal which can control DC / AC signal.
