# Fritzing sketch city (saved by Fritzing 0.9.3b)
breadboards: 1

parts:
  Εξάρτημα1 = Arduino Mega ADK (Rev3)
  HC-SR04_Sensor_1 = HC-SR04 Ultrasonic Distance Sensor
  HC-SR04_Sensor_2 = HC-SR04 Ultrasonic Distance Sensor
  HC-SR04_Sensor_3 = HC-SR04 Ultrasonic Distance Sensor
  e-radionica_com1 = LM393 LDR breakout [part_number=100027]
  PIR1 = PIR sensor
  LED1 = LED - 5mm [color="Red (633nm)" package="5 mm [THT]"]
  LED2 = LED - 5mm [color="Red (633nm)" package="5 mm [THT]"]
  LED3 = LED - 5mm [color="Red (633nm)" package="5 mm [THT]"]
  LED4 = LED - 5mm [color="Red (633nm)" package="5 mm [THT]"]
  LED5 = LED - 5mm [color="Red (633nm)" package="5 mm [THT]"]
  LED6 = LED - 5mm [color="Red (633nm)" package="5 mm [THT]"]
  WhiteLEDmodule1 = WhiteLEDmodule
  Εξάρτημα2 = Bluetooth HC-05 Macho
  R1 = Resistor [tolerance=±5% resistance=220 package=THT]
  R2 = Resistor [tolerance=±5% resistance=220 package=THT]
  R3 = Resistor [tolerance=±5% resistance=220 package=THT]
  R4 = Resistor [tolerance=±5% resistance=220 package=THT]
  R5 = Resistor [tolerance=±5% resistance=220 package=THT]
  R6 = Resistor [tolerance=±5% resistance=220 package=THT]
  KY-1 = Keyes Relay [package=THT]
  M1 = DC Motor
  Power_plug1 = Power plug

nets:
  N1: Εξάρτημα1.A10, e-radionica_com1.AO
  N2: Εξάρτημα1.D19/RX1, Εξάρτημα2.TXD
  N3: Εξάρτημα1.D18/TX1, Εξάρτημα2.RXD
  N4: Εξάρτημα1.D12_PWM, KY-1.signal
  VCC: Εξάρτημα1.5V, HC-SR04_Sensor_1.VCC, HC-SR04_Sensor_2.VCC, HC-SR04_Sensor_3.VCC, e-radionica_com1.VCC, PIR1.VDD, LED1.cathode, WhiteLEDmodule1.POWER, Εξάρτημα2.VCC, KY-1.power
  N5: Εξάρτημα1.D22, HC-SR04_Sensor_1.ECHO
  N6: Εξάρτημα1.D24, HC-SR04_Sensor_1.TRIG
  N7: Εξάρτημα1.D26, HC-SR04_Sensor_2.ECHO
  N8: Εξάρτημα1.D28, HC-SR04_Sensor_2.TRIG
  N9: Εξάρτημα1.D30, HC-SR04_Sensor_3.ECHO
  N10: Εξάρτημα1.D32, HC-SR04_Sensor_3.TRIG
  N11: Εξάρτημα1.D34, PIR1.SIG
  N12: Εξάρτημα1.D36, R1.Pin_0
  N13: Εξάρτημα1.D38, R2.Pin_0
  N14: Εξάρτημα1.D40, R3.Pin_0
  N15: Εξάρτημα1.D42, R4.Pin_0
  N16: Εξάρτημα1.D44, R5.Pin_0
  N17: Εξάρτημα1.D46, R6.Pin_0
  N18: Εξάρτημα1.D48, WhiteLEDmodule1.INPUT
  GND: Εξάρτημα1.GND, HC-SR04_Sensor_1.GND, HC-SR04_Sensor_2.GND, HC-SR04_Sensor_3.GND, e-radionica_com1.GND, PIR1.GND, LED2.cathode, LED3.cathode, LED4.cathode, LED5.anode, LED6.cathode, WhiteLEDmodule1.GND, Εξάρτημα2.GND, KY-1.ground
  N19: LED1.anode, R1.Pin_1
  N20: LED2.anode, R2.Pin_1
  N21: LED3.anode, R3.Pin_1
  N22: LED4.anode, R4.Pin_1
  N23: LED5.cathode, R5.Pin_1
  N24: LED6.anode, R6.Pin_1
  N25: KY-1.C, Power_plug1.GND
  N26: KY-1.NO, M1.pin_2
  N27: M1.pin_1, Power_plug1.VCC

custom parts:
  Keyes Relay: The Keyes 5V relay module is suitable for SCM development, home appliance control. It uses a 5V~12V TIL control signal which can control DC / AC signal.
